// Logisim project exerc-2.circ as structural Verilog
module ula (
);

  // AND_Gate and_1 is placed but not wired
  // OR_Gate or_1 is placed but not wired
  // NAND_Gate nand_1 is placed but not wired
  // XOR_Gate xor_1 is placed but not wired
endmodule
